// Digital circuit CPU 4.dig as structural Verilog
module CPU_4 (
  input  Clock,
  output [7:0] out_1,
  output CLK1,
  output CLK2
);

  wire _74245_1_p13, _74245_1_p14, _74245_1_p15, _74245_1_p16, _74245_1_p17, _74245_1_p18, _74245_1_p19,
       _74245_1_p20, and_1_out, and_2_out, and_7_out, and_8_out, bussplitter_1_d0, bussplitter_1_d1,
       bussplitter_1_d2, bussplitter_1_d3, bussplitter_1_d4, bussplitter_1_d5, bussplitter_1_d6,
       bussplitter_1_d7, C_SEL, CARRY, demultiplexer_1_out_0, demultiplexer_1_out_1, demultiplexer_1_out_2,
       demultiplexer_1_out_3, demultiplexer_2_out_1, demultiplexer_2_out_2, demultiplexer_2_out_3,
       demultiplexer_4_out_1, demultiplexer_4_out_2, demultiplexer_4_out_3, demultiplexer_4_out_4,
       demultiplexer_5_out_4, JMP_C, JMP_EN, JMP_POS, JMP_Z, multiplexer_2_out, nA_DOUT, nA_ST, nDISP_ST,
       nMAR_ST, nMEM_DOUT, nMEM_ST, not_1_out, not_7_out, not_8_out, not_9_out, not_10_out, not_17_out,
       not_18_out, nPC_ST, nROM_DOUT, nSUM_DOUT, nSUM_ST, or_1_out, or_3_out, t_ff_1_nq, t_ff_1_q, ZERO;
  wire [1:0] and_9_out, JMP_SEL, nor_1_out, nor_2_out;
  wire [2:0] CTRL_q, DOUT, ST;
  wire [2:2] demultiplexer_3_out_1, not_15_out;
  wire [7:0] A_q, add_1_s, ADS, DATA, MAR_q, MEM__64x8_d, PC_out, SUM_q;
  wire [7:7] CTRL_q_2;
  wire [15:0] rom_1_d;

  CounterPreset #(.Bits(8)) PC (
    .en(~1'b0), .C(CLK2), .dir(1'b0), .in(ADS), .ld(~nPC_ST), .clr(1'b0), .out(PC_out));  // open: ovf
  Demultiplexer #(.Selector_Bits(3)) demultiplexer_1 (
    .sel(DOUT), .in(1'b1), .out_0(demultiplexer_1_out_0), .out_1(demultiplexer_1_out_1),
    .out_2(demultiplexer_1_out_2), .out_3(demultiplexer_1_out_3));  // open: out_4, out_5, out_6, out_7
  not not_1 (not_1_out, Clock);
  PullDown pulldown_1 (.out(Clock));
  ROM #(.AddrBits(8), .Bits(16)) rom_1 (.A(PC_out), .sel(1'b1), .D(rom_1_d));
  not not_2 (nA_DOUT, demultiplexer_1_out_0);
  not not_3 (nMEM_DOUT, demultiplexer_1_out_1);
  not not_4 (nSUM_DOUT, demultiplexer_1_out_2);
  not not_5 (nROM_DOUT, demultiplexer_1_out_3);
  and and_1 (and_1_out, ~JMP_C, CARRY);  // And
  and and_2 (and_2_out, ~JMP_Z, ZERO);  // And
  T_FF #(.withEnable("false")) t_ff_1 (.C(not_1_out), .Q(t_ff_1_q), .nQ(t_ff_1_nq));
  and and_3 (CLK1, Clock, t_ff_1_q);
  and and_4 (CLK2, t_ff_1_nq, Clock);
  D_FF #(.Bits(16)) CTRL (.D(rom_1_d), .C(CLK1), .Q({ADS, CTRL_q_2[7], C_SEL, CTRL_q, DOUT}));  // open: nQ
  Demultiplexer #(.Selector_Bits(2)) demultiplexer_2 (
    .sel(JMP_SEL), .in(1'b1), .out_1(demultiplexer_2_out_1), .out_2(demultiplexer_2_out_2),
    .out_3(demultiplexer_2_out_3));  // open: out_0
  or or_1 (or_1_out, and_1_out, and_2_out);
  not not_6 (JMP_C, demultiplexer_2_out_1);
  not not_7 (not_7_out, demultiplexer_2_out_2);
  not not_8 (not_8_out, demultiplexer_2_out_3);
  not not_9 (not_9_out, or_1_out);
  assign DATA = ~nROM_DOUT ? ADS : 8'bz;  // DriverInvSel driverinvsel_1
  and and_5 (JMP_POS, not_7_out, JMP_C);
  Multiplexer multiplexer_1 (.sel(JMP_POS), .in_0(or_1_out), .in_1(not_9_out), .out(JMP_EN));
  Demultiplexer #(.Bits(3)) demultiplexer_3 (
    .sel(CTRL_q_2[7]), .in(CTRL_q), .out_0(ST), .out_1({demultiplexer_3_out_1[2], JMP_SEL}));
  and and_6 (JMP_Z, not_8_out, not_7_out);
  not not_10 (not_10_out, CTRL_q_2[7]);
  or or_2 (nPC_ST, not_10_out, JMP_EN);
  Demultiplexer #(.Selector_Bits(3)) demultiplexer_4 (
    .sel(ST), .in(1'b1), .out_1(demultiplexer_4_out_1), .out_2(demultiplexer_4_out_2),
    .out_3(demultiplexer_4_out_3), .out_4(demultiplexer_4_out_4));  // open: out_0, out_5, out_6, out_7
  Register #(.Bits(8)) DISP (.D(DATA), .C(CLK2), .en(~nDISP_ST), .Q(out_1));
  not not_11 (nA_ST, demultiplexer_4_out_1);
  not not_12 (nMEM_ST, demultiplexer_4_out_2);
  not not_13 (nSUM_ST, demultiplexer_4_out_3);
  not not_14 (nMAR_ST, demultiplexer_4_out_4);
  Register #(.Bits(8)) A (.D(DATA), .C(CLK2), .en(~nA_ST), .Q(A_q));
  assign DATA = ~nA_DOUT ? A_q : 8'bz;  // DriverInvSel driverinvsel_2
  Multiplexer multiplexer_2 (.sel(C_SEL), .in_0(1'b0), .in_1(CARRY), .out(multiplexer_2_out));
  Register #(.Bits(8)) MAR (.D(DATA), .C(CLK2), .en(~nMAR_ST), .Q(MAR_q));
  and and_7 (and_7_out, nMEM_DOUT, nMEM_ST);
  Add #(.Bits(8)) add_1 (.a(A_q), .b(DATA), .c_i(multiplexer_2_out), .s(add_1_s), .c_o(and_9_out[0]));
  not not_15 (not_15_out[2], nMEM_ST);
  or or_3 (or_3_out, 1'b0, MAR_q[6]);
  and and_8 (and_8_out, MAR_q[6], and_7_out);
  assign nor_1_out = ~(add_1_s[7:6] | add_1_s[5:4]);  // NOr nor_1, 2 bits wide
  assign nor_2_out = ~(add_1_s[3:2] | add_1_s[1:0]);  // NOr nor_2, 2 bits wide
  Demultiplexer #(.Selector_Bits(3)) demultiplexer_5 (
    .sel({not_15_out[2], MAR_q[1:0]}), .in(and_8_out), .out_4(demultiplexer_5_out_4));  // open: out_0, out_1, out_2, out_3, out_5, out_6, out_7
  RAMSinglePortSel #(.AddrBits(6), .Bits(8)) MEM__64x8 (
    .A(MAR_q[5:0]), .CS(~or_3_out), .WE(~nMEM_ST), .OE(~nMEM_DOUT), .D(MEM__64x8_d));
  not not_16 (nDISP_ST, demultiplexer_5_out_4);
  and and_9 (and_9_out[1], nor_1_out[0], nor_1_out[1], nor_2_out[0], nor_2_out[1]);
  PullDown #(.Bits(8)) pulldown_2 (.out(MEM__64x8_d));
  BusSplitter #(.Bits(8)) bussplitter_1 (
    .D(MEM__64x8_d), .OE(not_17_out), .D0(bussplitter_1_d0), .D1(bussplitter_1_d1), .D2(bussplitter_1_d2),
    .D3(bussplitter_1_d3), .D4(bussplitter_1_d4), .D5(bussplitter_1_d5), .D6(bussplitter_1_d6),
    .D7(bussplitter_1_d7));
  not not_17 (not_17_out, nMEM_DOUT);
  PullDown pulldown_3 (.out(bussplitter_1_d0));
  PullDown pulldown_4 (.out(bussplitter_1_d1));
  PullDown pulldown_5 (.out(bussplitter_1_d2));
  PullDown pulldown_6 (.out(bussplitter_1_d3));
  PullDown pulldown_7 (.out(bussplitter_1_d4));
  PullDown pulldown_8 (.out(bussplitter_1_d5));
  PullDown pulldown_9 (.out(bussplitter_1_d6));
  not not_18 (not_18_out, nMEM_DOUT);
  PullDown pulldown_10 (.out(bussplitter_1_d7));
  Register #(.Bits(2)) CZ (.D(and_9_out), .C(CLK2), .en(~nSUM_ST), .Q({ZERO, CARRY}));
  Register #(.Bits(8)) SUM (.D(add_1_s), .C(CLK2), .en(~nSUM_ST), .Q(SUM_q));
  // _74245 _74245_1: pin names not known; wires that end beside it: not_18_out, 1'b1, 1'b0, bussplitter_1_d0, bussplitter_1_d1, bussplitter_1_d2, bussplitter_1_d3, bussplitter_1_d4, bussplitter_1_d5, bussplitter_1_d6, bussplitter_1_d7, 1'b0, _74245_1_p13, _74245_1_p14, _74245_1_p15, _74245_1_p16, _74245_1_p17, _74245_1_p18, _74245_1_p19, _74245_1_p20
  assign DATA = ~nSUM_DOUT ? SUM_q : 8'bz;  // DriverInvSel driverinvsel_3
  PullDown pulldown_11 (.out(_74245_1_p20));
  PullDown pulldown_12 (.out(_74245_1_p19));
  PullDown pulldown_13 (.out(_74245_1_p18));
  PullDown pulldown_14 (.out(_74245_1_p17));
  BusSplitter #(.Bits(8)) bussplitter_2 (
    .D(DATA), .OE(nMEM_DOUT), .D0(_74245_1_p13), .D1(_74245_1_p14), .D2(_74245_1_p15), .D3(_74245_1_p16),
    .D4(_74245_1_p17), .D5(_74245_1_p18), .D6(_74245_1_p19), .D7(_74245_1_p20));
  PullDown pulldown_15 (.out(_74245_1_p16));
  PullDown pulldown_16 (.out(_74245_1_p15));
  PullDown pulldown_17 (.out(_74245_1_p14));
  PullDown pulldown_18 (.out(_74245_1_p13));

  // Other names for the same wires on the sheet: CLK_1 = CLK1; CLK_2 = CLK2

  // Notes on the sheet:
  //   Clock: Hz: 200
  //   CTRL
endmodule
